# Fritzing sketch Schematic (saved by Fritzing 0.8.3b)
breadboards: 1

parts:
  Teensy1 = Teensy 2.0
  CapSensor = female pin header, 1 pin [form="♀ (female)"]
  R1 = Resistor [tolerance=±5% resistance=10M package=THT]
  LED1_PWR = LED - 5mm [color="Green (565nm)" package="5 mm [THT]"]
  R2 = Resistor [tolerance=±5% resistance=300 package=THT]
  LED1_OK = LED - 5mm [color="Green (565nm)" package="5 mm [THT]"]
  R3 = Resistor [tolerance=±5% resistance=300 package=THT]
  LED1_FAIL = LED - 5mm [color="Green (565nm)" package="5 mm [THT]"]
  R4 = Resistor [tolerance=±5% resistance=300 package=THT]
  J1 = Piezo Speaker

nets:
  N1: Teensy1.GND, R2.Pin_0, R3.Pin_0, R4.Pin_0, J1.pin2
  N2: Teensy1.D2, R1.Pin_0
  N3: Teensy1.D6, LED1_PWR.anode
  N4: Teensy1.F7, CapSensor.pin1, R1.Pin_1
  N5: LED1_PWR.cathode, R2.Pin_1
  N6: LED1_OK.cathode, R3.Pin_1
  N7: LED1_FAIL.cathode, R4.Pin_1
